// Digital circuit REG MUL 34 V1.dig as structural Verilog
module REG_MUL_34_V1 (
  input  I0,
  input  I1,
  input  I2,
  input  I3,
  input  I4,
  input  I5,
  input  I6,
  input  I7,
  input  I8,
  input  I9,
  input  I10,
  input  I11,
  input  I12,
  input  I13,
  input  I14,
  input  I15,
  input  I16,
  input  I17,
  input  I18,
  input  I19,
  input  I20,
  input  I21,
  input  I22,
  input  I23,
  input  I24,
  input  I25,
  input  I26,
  input  I27,
  input  I28,
  input  I29,
  input  I30,
  input  I31,
  input  I32,
  input  I33,
  input  CLK,
  input  RST,
  input  EN,
  output Q14,
  output Q15,
  output Q16,
  output Q17,
  output Q18,
  output Q19,
  output Q20,
  output Q21,
  output Q22,
  output Q23,
  output Q24,
  output Q25,
  output Q26,
  output Q27,
  output Q28,
  output Q29,
  output Q30,
  output Q31,
  output Q32,
  output Q33,
  output Q0,
  output Q1,
  output Q2,
  output Q3,
  output Q4,
  output Q5,
  output Q6,
  output Q7,
  output Q8,
  output Q9,
  output Q10,
  output Q11,
  output Q12,
  output Q13
);

  // _1_BIT_REG_V1 D0: pin names not known; wires that end beside it: CLK, RST, EN, I0, Q0
  // _1_BIT_REG_V1 D2: pin names not known; wires that end beside it: CLK, RST, EN, I2, Q2
  // _1_BIT_REG_V1 D4: pin names not known; wires that end beside it: CLK, RST, EN, I4, Q4
  // _1_BIT_REG_V1 D6: pin names not known; wires that end beside it: CLK, RST, EN, I6, Q6
  // _1_BIT_REG_V1 D8: pin names not known; wires that end beside it: CLK, RST, EN, I8, Q8
  // _1_BIT_REG_V1 D10: pin names not known; wires that end beside it: CLK, RST, EN, I10, Q10
  // _1_BIT_REG_V1 D12: pin names not known; wires that end beside it: CLK, RST, EN, I12, Q12
  // _1_BIT_REG_V1 D14: pin names not known; wires that end beside it: CLK, RST, EN, I14, Q14
  // _1_BIT_REG_V1 D16: pin names not known; wires that end beside it: CLK, RST, EN, I16, Q16
  // _1_BIT_REG_V1 D18: pin names not known; wires that end beside it: CLK, RST, EN, I18, Q18
  // _1_BIT_REG_V1 D20: pin names not known; wires that end beside it: CLK, RST, EN, I20, Q20
  // _1_BIT_REG_V1 D22: pin names not known; wires that end beside it: CLK, RST, EN, I22, Q22
  // _1_BIT_REG_V1 D24: pin names not known; wires that end beside it: CLK, RST, EN, I24, Q24
  // _1_BIT_REG_V1 D26: pin names not known; wires that end beside it: CLK, RST, EN, I26, Q26
  // _1_BIT_REG_V1 D28: pin names not known; wires that end beside it: CLK, RST, EN, I28, Q28
  // _1_BIT_REG_V1 D30: pin names not known; wires that end beside it: CLK, RST, EN, I30, Q30
  // _1_BIT_REG_V1 D32: pin names not known; wires that end beside it: CLK, RST, EN, I32, Q32
  // _1_BIT_REG_V1 D1: pin names not known; wires that end beside it: CLK, RST, EN, I1, Q1
  // _1_BIT_REG_V1 D3: pin names not known; wires that end beside it: CLK, RST, EN, I3, Q3
  // _1_BIT_REG_V1 D5: pin names not known; wires that end beside it: CLK, RST, EN, I5, Q5
  // _1_BIT_REG_V1 D7: pin names not known; wires that end beside it: CLK, RST, EN, I7, Q7
  // _1_BIT_REG_V1 D9: pin names not known; wires that end beside it: CLK, RST, EN, I9, Q9
  // _1_BIT_REG_V1 D11: pin names not known; wires that end beside it: CLK, RST, EN, I11, Q11
  // _1_BIT_REG_V1 D13: pin names not known; wires that end beside it: CLK, RST, EN, I13, Q13
  // _1_BIT_REG_V1 D15: pin names not known; wires that end beside it: CLK, RST, EN, I15, Q15
  // _1_BIT_REG_V1 D17: pin names not known; wires that end beside it: CLK, RST, EN, I17, Q17
  // _1_BIT_REG_V1 D19: pin names not known; wires that end beside it: CLK, RST, EN, I19, Q19
  // _1_BIT_REG_V1 D21: pin names not known; wires that end beside it: CLK, RST, EN, I21, Q21
  // _1_BIT_REG_V1 D23: pin names not known; wires that end beside it: CLK, RST, EN, I23, Q23
  // _1_BIT_REG_V1 D25: pin names not known; wires that end beside it: CLK, RST, EN, I25, Q25
  // _1_BIT_REG_V1 D27: pin names not known; wires that end beside it: CLK, RST, EN, I27, Q27
  // _1_BIT_REG_V1 D29: pin names not known; wires that end beside it: CLK, RST, EN, I29, Q29
  // _1_BIT_REG_V1 D31: pin names not known; wires that end beside it: CLK, RST, EN, I31, Q31
  // _1_BIT_REG_V1 D33: pin names not known; wires that end beside it: CLK, RST, EN, I33, Q33
endmodule
